# Fritzing sketch tft_side_schematic (saved by Fritzing 0.9.6b)

parts:
  BAT1 = Battery Holders [package=lipo-1100mAh]
  LCD3 = 2.8" SPI TFT Module [part_number=MSP2807]
  LED1 = LEDs [package=led10mm]
  S5 = Round Pushbutton
  S6 = Round Pushbutton
  R2 = Resistor [tolerance=±5% resistance=6.8k package="0805 [SMD]"]
  R3 = Resistor [tolerance=±5% resistance=6.8k package="0805 [SMD]"]

nets:
  N1: BAT1.+, LCD3.pin14, R2.Pin_0, R3.Pin_0
  N2: BAT1.-, LED1.A, S5.leg0, S6.leg1
  N3: LCD3.pin2, LED1.C
  N4: LCD3.pin6, S6.leg0, R3.Pin_1
  N5: LCD3.pin7, S5.leg1, R2.Pin_1

custom parts:
  2.8" SPI TFT Module: A generic 2.8 inch LCD TFT 320x240 display with touchscreen and SD card slot. Uses the ILI9341 controller, like the Adafruit displays of this size uses.
